// Logisim project STMicroelectronics_counter_3bits_logisim_evolution.circ as structural Verilog: 1 circuit, main circuit main
module main (
  input  user_button,
  input  play_clk
);

  wire and_1_out, and_2_out, and_3_out, and_4_out, d_ff_1_qn, LUT1_out, LUT2_out, LUT3_out;
  wire [0:0] d_ff_2_q, d_ff_3_q, d_ff_4_q;

  D_Flip_Flop d_ff_1 (.D(user_button), .clk(play_clk), .Qn(d_ff_1_qn));  // open: Q, preset, reset
  and and_1 (and_1_out, user_button, d_ff_1_qn);
  and and_2 (and_2_out, and_1_out, play_clk);
  and and_3 (and_3_out, and_1_out, play_clk);
  and and_4 (and_4_out, and_1_out, play_clk);
  PLA #(.in_width(4), .out_width(1), .\table ("0000 1 # !in\n0001 0 # !in")) LUT1 (
    .in({3'b000, d_ff_2_q[0]}), .out(LUT1_out));
  D_Flip_Flop d_ff_2 (.D(LUT1_out), .clk(and_2_out), .Q(d_ff_2_q[0]));  // open: Qn, preset, reset
  PLA #(.in_width(4), .out_width(1), .\table ("0000 0 # Q0^Q1\n0001 1 # Q0^Q1\n0010 1 # Q0^Q1\n0011 0 # Q0^Q1")) LUT2 (
    .in({2'b00, d_ff_2_q[0], d_ff_3_q[0]}), .out(LUT2_out));
  D_Flip_Flop d_ff_3 (.D(LUT2_out), .clk(and_3_out), .Q(d_ff_3_q[0]));  // open: Qn, preset, reset
  PLA #(.in_width(4), .out_width(1), .\table ("0000 0 # Q2^(Q0&Q1)\n0001 1 # Q2^(Q0&Q1)\n0010 0 # Q2^(Q0&Q1)\n0011 1 # Q2^(Q0&Q1)\n0100 0 # Q2^(Q0&Q1)\n0101 1 # Q2^(Q0&Q1)\n0110 1 # Q2^(Q0&Q1)\n0111 0 # Q2^(Q0&Q1)")) LUT3 (
    .in({1'b0, d_ff_2_q[0], d_ff_3_q[0], d_ff_4_q[0]}), .out(LUT3_out));
  D_Flip_Flop d_ff_4 (.D(LUT3_out), .clk(and_4_out), .Q(d_ff_4_q[0]));  // open: Qn, preset, reset
  // NoConnect on LUT1_out
  // NoConnect on LUT2_out
  // NoConnect on LUT3_out
  LED Q0 (.in(d_ff_2_q[0]));
  LED Q1 (.in(d_ff_3_q[0]));
  LED Q2 (.in(d_ff_4_q[0]));

  // Notes on the sheet:
  //   EDGE_DETECTOR
  //   PLAY_IN_AFTER_EDGE_DETECT
  //   LUT1_DIRECT_OUTPUT
  //   LUT1_REGISTERED_OUTPUT
  //   LUT2_DIRECT_OUTPUT
  //   LUT2_REGISTERED_OUTPUT
  //   LUT3_DIRECT_OUTPUT
  //   LUT3_REGISTERED_OUTPUT
endmodule
