// Logisim project STMicroelectronics_emergency_alarm_logisim_evolution.circ as structural Verilog: 1 circuit, main circuit main
module main (
  input  user_button,
  input  play_clk
);

  wire and_1_out, and_2_out, and_3_out, and_4_out, and_5_out, and_6_out, and_7_out, and_8_out, and_9_out,
       and_10_out, and_11_out, and_12_out, and_13_out, and_14_out, d_ff_1_qn, d_ff_7_q, d_ff_9_q, d_ff_10_q,
       d_ff_11_q, d_ff_12_q, d_ff_13_q, d_ff_14_q, LUT0_out, LUT1_out, LUT2_out, LUT3_out, LUT5_out,
       LUT11_out, LUT15_out;
  wire [1:0] d_ff_2_q;
  wire [1:1] d_ff_4_q, LUT4_out;
  wire [3:0] d_ff_5_q, LUT8_out;

  D_Flip_Flop d_ff_1 (.D(user_button), .clk(play_clk), .Qn(d_ff_1_qn));  // open: Q, preset, reset
  and and_1 (and_1_out, user_button, d_ff_1_qn);
  PLA #(.in_width(4), .out_width(1), .\table ("0000 1 # !in\n0001 0 # !in")) LUT15 (
    .in({3'b000, d_ff_2_q[0]}), .out(LUT15_out));
  D_Flip_Flop d_ff_2 (.D(LUT15_out), .clk(and_2_out), .Q(d_ff_2_q[0]));  // open: Qn, preset, reset
  and and_2 (and_2_out, and_1_out, play_clk);
  // NoConnect on LUT15_out
  PLA #(.in_width(4), .out_width(1), .\table ("0000 1 # !in\n0001 0 # !in")) LUT0 (
    .in({3'b000, d_ff_5_q[0]}), .out(LUT0_out));
  D_Flip_Flop d_ff_3 (.D(LUT0_out), .clk(and_3_out), .Q(d_ff_5_q[0]));  // open: Qn, preset, reset
  and and_3 (and_3_out, d_ff_2_q[0], play_clk);
  PLA #(.in_width(4), .out_width(1), .\table ("0000 0 # Q0^Q1\n0001 1 # Q0^Q1\n0010 1 # Q0^Q1\n0011 0 # Q0^Q1")) LUT1 (
    .in({2'b00, d_ff_5_q[0], d_ff_4_q[1]}), .out(LUT1_out));
  D_Flip_Flop d_ff_4 (.D(LUT1_out), .clk(and_4_out), .Q(d_ff_4_q[1]));  // open: Qn, preset, reset
  and and_4 (and_4_out, d_ff_2_q[0], play_clk);
  PLA #(.in_width(4), .out_width(1), .\table ("0000 0 # Q2^(Q0&Q1)\n0001 1 # Q2^(Q0&Q1)\n0010 0 # Q2^(Q0&Q1)\n0011 1 # Q2^(Q0&Q1)\n0100 0 # Q2^(Q0&Q1)\n0101 1 # Q2^(Q0&Q1)\n0110 1 # Q2^(Q0&Q1)\n0111 0 # Q2^(Q0&Q1)")) LUT2 (
    .in({1'b0, d_ff_5_q[0], d_ff_4_q[1], d_ff_5_q[1]}), .out(LUT2_out));
  D_Flip_Flop d_ff_5 (.D(LUT2_out), .clk(and_5_out), .Q(d_ff_5_q[1]));  // open: Qn, preset, reset
  and and_5 (and_5_out, d_ff_2_q[0], play_clk);
  PLA #(.in_width(4), .out_width(1), .\table ("0000 0 # Q3^(Q0&Q1&Q2)\n0001 1 # Q3^(Q0&Q1&Q2)\n0010 0 # Q3^(Q0&Q1&Q2)\n0011 1 # Q3^(Q0&Q1&Q2)\n0100 0 # Q3^(Q0&Q1&Q2)\n0101 1 # Q3^(Q0&Q1&Q2)\n0110 0 # Q3^(Q0&Q1&Q2)\n0111 1 # Q3^(Q0&Q1&Q2)\n1000 0 # Q3^(Q0&Q1&Q2)\n1001 1 # Q3^(Q0&Q1&Q2)\n1010 0 # Q3^(Q0&Q1&Q2)\n1011 1 # Q3^(Q0&Q1&Q2)\n1100 0 # Q3^(Q0&Q1&Q2)\n1101 1 # Q3^(Q0&Q1&Q2)\n1110 1 # Q3^(Q0&Q1&Q2)\n1111 0 # Q3^(Q0&Q1&Q2)")) LUT3 (
    .in({d_ff_5_q[1:0], d_ff_4_q[1], d_ff_5_q[2]}), .out(LUT3_out));
  D_Flip_Flop d_ff_6 (.D(LUT3_out), .clk(and_6_out), .Q(d_ff_5_q[2]));  // open: Qn, preset, reset
  and and_6 (and_6_out, d_ff_2_q[0], play_clk);
  PLA #(.in_width(4), .out_width(1), .\table ("0000 0 # Q0&Q1&Q2&Q3\n0001 0 # Q0&Q1&Q2&Q3\n0010 0 # Q0&Q1&Q2&Q3\n0011 0 # Q0&Q1&Q2&Q3\n0100 0 # Q0&Q1&Q2&Q3\n0101 0 # Q0&Q1&Q2&Q3\n0110 0 # Q0&Q1&Q2&Q3\n0111 0 # Q0&Q1&Q2&Q3\n1000 0 # Q0&Q1&Q2&Q3\n1001 0 # Q0&Q1&Q2&Q3\n1010 0 # Q0&Q1&Q2&Q3\n1011 0 # Q0&Q1&Q2&Q3\n1100 0 # Q0&Q1&Q2&Q3\n1101 0 # Q0&Q1&Q2&Q3\n1110 0 # Q0&Q1&Q2&Q3\n1111 1 # Q0&Q1&Q2&Q3")) LUT4 (
    .in({d_ff_5_q[2:0], d_ff_4_q[1]}), .out(LUT4_out[1]));
  D_Flip_Flop d_ff_7 (.D(LUT4_out[1]), .clk(and_7_out), .Q(d_ff_7_q));  // open: Qn, preset, reset
  and and_7 (and_7_out, 1'b0, play_clk);
  PLA #(.in_width(4), .out_width(1), .\table ("0000 0 # Q4^(LUT4)\n0001 1 # Q4^(LUT4)\n0010 1 # Q4^(LUT4)\n0011 0 # Q4^(LUT4)")) LUT5 (
    .in({2'b00, LUT4_out[1], d_ff_5_q[3]}), .out(LUT5_out));
  D_Flip_Flop d_ff_8 (.D(LUT5_out), .clk(and_8_out), .Q(d_ff_5_q[3]));  // open: Qn, preset, reset
  and and_8 (and_8_out, d_ff_2_q[0], play_clk);
  // NoConnect on LUT0_out
  // NoConnect on LUT1_out
  // NoConnect on LUT2_out
  // NoConnect on LUT3_out
  // NoConnect on d_ff_7_q
  // NoConnect on LUT5_out
  buf and_9 (and_9_out, 1'b1);  // AND_Gate
  buf and_10 (and_10_out, 1'b1);  // AND_Gate
  buf and_11 (and_11_out, 1'b1);  // AND_Gate
  buf and_12 (and_12_out, 1'b1);  // AND_Gate
  PLA #(.in_width(4), .out_width(1), .\table ("0000 1 # (!Q2 & !Q0) | (!Q4 & Q3 & !Q0)\n0001 0 # (!Q2 & !Q0) | (!Q4 & Q3 & !Q0)\n0010 0 # (!Q2 & !Q0) | (!Q4 & Q3 & !Q0)\n0011 0 # (!Q2 & !Q0) | (!Q4 & Q3 & !Q0)\n0100 1 # (!Q2 & !Q0) | (!Q4 & Q3 & !Q0)\n0101 0 # (!Q2 & !Q0) | (!Q4 & Q3 & !Q0)\n0110 1 # (!Q2 & !Q0) | (!Q4 & Q3 & !Q0)\n0111 0 # (!Q2 & !Q0) | (!Q4 & Q3 & !Q0)\n1000 1 # (!Q2 & !Q0) | (!Q4 & Q3 & !Q0)\n1001 0 # (!Q2 & !Q0) | (!Q4 & Q3 & !Q0)\n1010 0 # (!Q2 & !Q0) | (!Q4 & Q3 & !Q0)\n1011 0 # (!Q2 & !Q0) | (!Q4 & Q3 & !Q0)\n1100 1 # (!Q2 & !Q0) | (!Q4 & Q3 & !Q0)\n1101 0 # (!Q2 & !Q0) | (!Q4 & Q3 & !Q0)\n1110 0 # (!Q2 & !Q0) | (!Q4 & Q3 & !Q0)\n1111 0 # (!Q2 & !Q0) | (!Q4 & Q3 & !Q0)")) LUT8 (
    .in(d_ff_5_q), .out(LUT8_out[0]));
  D_Flip_Flop d_ff_9 (.D(LUT8_out[0]), .clk(and_9_out), .Q(d_ff_9_q));  // open: Qn, preset, reset
  PLA #(.in_width(4), .out_width(1), .\table ("0000 1 # (!Q4 & !Q1 & !Q0) | (!Q4 & Q3 & !Q1)\n0001 0 # (!Q4 & !Q1 & !Q0) | (!Q4 & Q3 & !Q1)\n0010 0 # (!Q4 & !Q1 & !Q0) | (!Q4 & Q3 & !Q1)\n0011 0 # (!Q4 & !Q1 & !Q0) | (!Q4 & Q3 & !Q1)\n0100 1 # (!Q4 & !Q1 & !Q0) | (!Q4 & Q3 & !Q1)\n0101 1 # (!Q4 & !Q1 & !Q0) | (!Q4 & Q3 & !Q1)\n0110 0 # (!Q4 & !Q1 & !Q0) | (!Q4 & Q3 & !Q1)\n0111 0 # (!Q4 & !Q1 & !Q0) | (!Q4 & Q3 & !Q1)\n1000 0 # (!Q4 & !Q1 & !Q0) | (!Q4 & Q3 & !Q1)\n1001 0 # (!Q4 & !Q1 & !Q0) | (!Q4 & Q3 & !Q1)\n1010 0 # (!Q4 & !Q1 & !Q0) | (!Q4 & Q3 & !Q1)\n1011 0 # (!Q4 & !Q1 & !Q0) | (!Q4 & Q3 & !Q1)\n1100 0 # (!Q4 & !Q1 & !Q0) | (!Q4 & Q3 & !Q1)\n1101 0 # (!Q4 & !Q1 & !Q0) | (!Q4 & Q3 & !Q1)\n1110 0 # (!Q4 & !Q1 & !Q0) | (!Q4 & Q3 & !Q1)\n1111 0 # (!Q4 & !Q1 & !Q0) | (!Q4 & Q3 & !Q1)")) LUT9 (
    .in({d_ff_5_q[3:2], d_ff_4_q[1], d_ff_5_q[0]}), .out(LUT8_out[1]));
  D_Flip_Flop d_ff_10 (.D(LUT8_out[1]), .clk(and_10_out), .Q(d_ff_10_q));  // open: Qn, preset, reset
  PLA #(.in_width(4), .out_width(1), .\table ("0000 0 # Q4 & !Q3 & !Q2 & !Q1\n0001 0 # Q4 & !Q3 & !Q2 & !Q1\n0010 0 # Q4 & !Q3 & !Q2 & !Q1\n0011 0 # Q4 & !Q3 & !Q2 & !Q1\n0100 0 # Q4 & !Q3 & !Q2 & !Q1\n0101 0 # Q4 & !Q3 & !Q2 & !Q1\n0110 0 # Q4 & !Q3 & !Q2 & !Q1\n0111 0 # Q4 & !Q3 & !Q2 & !Q1\n1000 1 # Q4 & !Q3 & !Q2 & !Q1\n1001 0 # Q4 & !Q3 & !Q2 & !Q1\n1010 0 # Q4 & !Q3 & !Q2 & !Q1\n1011 0 # Q4 & !Q3 & !Q2 & !Q1\n1100 0 # Q4 & !Q3 & !Q2 & !Q1\n1101 0 # Q4 & !Q3 & !Q2 & !Q1\n1110 0 # Q4 & !Q3 & !Q2 & !Q1\n1111 0 # Q4 & !Q3 & !Q2 & !Q1")) LUT12 (
    .in({d_ff_5_q[3:1], d_ff_4_q[1]}), .out(LUT8_out[2]));
  D_Flip_Flop d_ff_11 (.D(LUT8_out[2]), .clk(and_11_out), .Q(d_ff_11_q));  // open: Qn, preset, reset
  PLA #(.in_width(4), .out_width(1), .\table ("0000 0 # Q4 & !Q3 & Q1 & !Q0\n0001 0 # Q4 & !Q3 & Q1 & !Q0\n0010 0 # Q4 & !Q3 & Q1 & !Q0\n0011 0 # Q4 & !Q3 & Q1 & !Q0\n0100 0 # Q4 & !Q3 & Q1 & !Q0\n0101 0 # Q4 & !Q3 & Q1 & !Q0\n0110 0 # Q4 & !Q3 & Q1 & !Q0\n0111 0 # Q4 & !Q3 & Q1 & !Q0\n1000 0 # Q4 & !Q3 & Q1 & !Q0\n1001 0 # Q4 & !Q3 & Q1 & !Q0\n1010 1 # Q4 & !Q3 & Q1 & !Q0\n1011 0 # Q4 & !Q3 & Q1 & !Q0\n1100 0 # Q4 & !Q3 & Q1 & !Q0\n1101 0 # Q4 & !Q3 & Q1 & !Q0\n1110 0 # Q4 & !Q3 & Q1 & !Q0\n1111 0 # Q4 & !Q3 & Q1 & !Q0")) LUT13 (
    .in({d_ff_5_q[3:2], d_ff_4_q[1], d_ff_5_q[0]}), .out(LUT8_out[3]));
  D_Flip_Flop d_ff_12 (.D(LUT8_out[3]), .clk(and_12_out), .Q(d_ff_12_q));  // open: Qn, preset, reset
  // NoConnect on d_ff_9_q
  // NoConnect on d_ff_10_q
  // NoConnect on d_ff_11_q
  // NoConnect on d_ff_12_q
  buf and_13 (and_13_out, 1'b1);  // AND_Gate
  PLA #(.in_width(4), .out_width(1), .\table ("0000 0 # OR\n0001 1 # OR\n0010 1 # OR\n0011 1 # OR\n0100 1 # OR\n0101 1 # OR\n0110 1 # OR\n0111 1 # OR\n1000 1 # OR\n1001 1 # OR\n1010 1 # OR\n1011 1 # OR\n1100 1 # OR\n1101 1 # OR\n1110 1 # OR\n1111 1 # OR")) LUT10 (
    .in(LUT8_out), .out(d_ff_2_q[1]));
  D_Flip_Flop d_ff_13 (.D(d_ff_2_q[1]), .clk(and_13_out), .Q(d_ff_13_q));  // open: Qn, preset, reset
  // NoConnect on d_ff_13_q
  PLA #(.in_width(4), .out_width(1), .\table ("0000 0 # AND\n0001 0 # AND\n0010 0 # AND\n0011 1 # AND")) LUT11 (
    .in({2'b00, d_ff_2_q}), .out(LUT11_out));
  D_Flip_Flop d_ff_14 (.D(LUT11_out), .clk(and_14_out), .Q(d_ff_14_q));  // open: Qn, preset, reset
  buf and_14 (and_14_out, 1'b1);  // AND_Gate
  LED SOS (.in(LUT11_out));
  // NoConnect on d_ff_14_q

  // Notes on the sheet:
  //   Edge detector
  //   LUT15_DIRECT_OUTPUT
  //   LUT15_REGISTERED_OUTPUT
  //   LUT0_DIRECT_OUTPUT
  //   LUT0_REGISTERED_OUTPUT
  //   LUT1_DIRECT_OUTPUT
  //   LUT1_REGISTERED_OUTPUT
  //   LUT2_DIRECT_OUTPUT
  //   LUT2_REGISTERED_OUTPUT
  //   LUT3_DIRECT_OUTPUT
  //   LUT3_REGISTERED_OUTPUT
  //   LUT4_DIRECT_OUTPUT
  //   LUT4_REGISTERED_OUTPUT
  //   LUT5_DIRECT_OUTPUT
  //   LUT4_REGISTERED_OUTPUT
  //   Q0
  //   Q1
  //   Q2
  //   Q3
  //   Q4
  //   Q: 0 1 2 3 4
  //   Q: 0 1 2 3 4
  //   LUT8_DIRECT_OUTPUT
  //   LUT8_REGISTERED_OUTPUT
  //   LUT9_DIRECT_OUTPUT
  //   LUT9_REGISTERED_OUTPUT
  //   LUT12_DIRECT_OUTPUT
  //   LUT12_REGISTERED_OUTPUT
  //   LUT13_DIRECT_OUTPUT
  //   LUT13_REGISTERED_OUTPUT
  //   LUT10_DIRECT_OUTPUT
  //   LUT10_REGISTERED_OUTPUT
  //   LUT11_DIRECT_OUTPUT
  //   LUT11_REGISTERED_OUTPUT
endmodule
